// Logisim project ALU.circ as structural Verilog: 5 circuits, main circuit ALU
module ALU (
);

  wire [2:0] undriven_2;
  wire [15:0] demultiplexer_1_out0, demultiplexer_1_out1, demultiplexer_1_out2, demultiplexer_1_out3,
       demultiplexer_1_out4, demultiplexer_1_out5, demultiplexer_1_out6, demultiplexer_1_out7, undriven;

  Demultiplexer #(.select(3), .width(16)) demultiplexer_1 (
    .out0(demultiplexer_1_out0), .out1(demultiplexer_1_out1), .out2(demultiplexer_1_out2),
    .out3(demultiplexer_1_out3), .out4(demultiplexer_1_out4), .out5(demultiplexer_1_out5),
    .out6(demultiplexer_1_out6), .out7(demultiplexer_1_out7), .in(undriven), .sel(undriven_2), .en(1'b1));
endmodule

module _16_Bit_adder (
  input  [15:0] Input_a,
  input  Subtract,
  input  [15:0] Input_b,
  output [15:0] Sum
);

  wire n4_bit_adder_1_carry_out, n4_bit_adder_2_carry_out, n4_bit_adder_3_carry_out;

  _4_Bit_adder u_4_bit_adder_1 (
    .Input_a(Input_a[11:8]), .Carry_in(n4_bit_adder_2_carry_out), .Input_b(Input_b[11:8]), .Sum(Sum[11:8]),
    .Carry_out(n4_bit_adder_1_carry_out), .Subtract(Subtract));
  _4_Bit_adder u_4_bit_adder_2 (
    .Input_a(Input_a[15:12]), .Carry_in(1'b0), .Input_b(Input_b[15:12]), .Sum(Sum[15:12]),
    .Carry_out(n4_bit_adder_2_carry_out), .Subtract(Subtract));
  _4_Bit_adder u_4_bit_adder_3 (
    .Input_a(Input_a[7:4]), .Carry_in(n4_bit_adder_1_carry_out), .Input_b(Input_b[7:4]), .Sum(Sum[7:4]),
    .Carry_out(n4_bit_adder_3_carry_out), .Subtract(Subtract));
  _4_Bit_adder u_4_bit_adder_4 (
    .Input_a(Input_a[3:0]), .Carry_in(n4_bit_adder_3_carry_out), .Input_b(Input_b[3:0]), .Sum(Sum[3:0]),
    .Subtract(Subtract));  // open: Carry_out
endmodule

module _4_Bit_adder (
  input  [3:0] Input_a,
  input  Carry_in,
  input  Subtract,
  input  [3:0] Input_b,
  output [3:0] Sum,
  output Carry_out
);

  wire full_adder_1_carry_out, full_adder_2_carry_out, full_adder_3_carry_out, xor_1_out, xor_2_out,
       xor_3_out, xor_4_out;

  xor xor_1 (xor_1_out, Subtract, Input_b[0]);
  Full_adder full_adder_1 (
    .Input_a(Input_a[1]), .Input_b(xor_2_out), .Carry_in(full_adder_2_carry_out), .Sum(Sum[1]),
    .Carry_out(full_adder_1_carry_out));
  Full_adder full_adder_2 (
    .Input_a(Input_a[0]), .Input_b(xor_1_out), .Carry_in(Carry_in), .Sum(Sum[0]),
    .Carry_out(full_adder_2_carry_out));
  xor xor_2 (xor_2_out, Subtract, Input_b[1]);
  Full_adder full_adder_3 (
    .Input_a(Input_a[2]), .Input_b(xor_4_out), .Carry_in(full_adder_1_carry_out), .Sum(Sum[2]),
    .Carry_out(full_adder_3_carry_out));
  xor xor_3 (xor_3_out, Subtract, Input_b[3]);
  xor xor_4 (xor_4_out, Subtract, Input_b[2]);
  Full_adder full_adder_4 (
    .Input_a(Input_a[3]), .Input_b(xor_3_out), .Carry_in(full_adder_3_carry_out), .Sum(Sum[3]),
    .Carry_out(Carry_out));
endmodule

module Full_adder (
  input  Input_a,
  input  Input_b,
  input  Carry_in,
  output Sum,
  output Carry_out
);

  wire half_adder_1_carry, half_adder_1_sum, half_adder_2_carry;

  Half_adder half_adder_1 (.Input_a(Input_a), .Input_b(Input_b), .Sum(half_adder_1_sum), .Carry(half_adder_1_carry));
  Half_adder half_adder_2 (.Input_a(half_adder_1_sum), .Input_b(Carry_in), .Sum(Sum), .Carry(half_adder_2_carry));
  or or_1 (Carry_out, half_adder_2_carry, half_adder_1_carry);
endmodule

module Half_adder (
  input  Input_a,
  input  Input_b,
  output Sum,
  output Carry
);

  xor xor_1 (Sum, Input_a, Input_b);
  and and_1 (Carry, Input_a, Input_b);
endmodule
