// Logisim project Main bus.circ as structural Verilog: 1 circuit, main circuit Main bus
module Main_bus (
  input  [15:0] in_1,
  input  in_2,
  input  in_3,
  input  in_4,
  input  in_5,
  input  in_6,
  input  [2:0] in_7,
  input  in_8
);

  wire and_1_out, and_2_out, IRBuf, MARBuf, PCEn;
  wire [2:0] ExPhase, GenPhase;
  wire [15:0] Accumulator_register_q, alu_1_out_4, controlled_buffer_1_out, controlled_buffer_2_out,
       controlled_buffer_3_out, controlled_buffer_6_out, controlled_buffer_7_out, controlled_buffer_8_out,
       Input_register_2_q, Input_register_q, Instruction_register_q, Memory_access_register_q,
       Output_register_q, Program_counter_q, ram_1_data;

  Counter #(.width(3), .max('h7)) counter_1 (
    .count(1'b1), .Q(GenPhase), .clk(in_8), .clr(and_1_out));  // open: load, D, carry
  and and_1 (and_1_out, GenPhase[2], ~GenPhase[1], ~GenPhase[0]);  // AND_Gate
  Counter #(.width(3), .max('h7)) counter_2 (
    .count(1'b1), .Q(ExPhase), .clk(in_8), .clr(and_2_out));  // open: load, D, carry
  and and_2 (and_2_out, ExPhase[2], ExPhase[1], ExPhase[0]);
  Register #(.width(16)) Memory_access_register (
    .D(controlled_buffer_1_out), .en(1'b1), .Q(Memory_access_register_q), .clk(in_8));  // open: clr
  Register #(.width(16)) Instruction_register (
    .D(controlled_buffer_2_out), .en(1'b1), .Q(Instruction_register_q), .clk(in_8));  // open: clr
  Counter #(.width(16), .max('hffff)) Program_counter (
    .count(PCEn), .Q(Program_counter_q), .clk(in_8));  // open: load, D, carry, clr
  assign controlled_buffer_1_out = MARBuf ? controlled_buffer_3_out : 16'bz;  // Controlled_Buffer controlled_buffer_1
  RAM #(.addrWidth(16), .dataWidth(16)) ram_1 (
    .addr(Memory_access_register_q), .data(ram_1_data), .clk(in_8), .ld(1'b1));  // open: sel, clr
  assign controlled_buffer_2_out = IRBuf ? controlled_buffer_3_out : 16'bz;  // Controlled_Buffer controlled_buffer_2
  ROM #(.addrWidth(4), .dataWidth(16)) rom_1 (.addr(Instruction_register_q[3:0]));  // open: data, sel
  nor nor_1 (MARBuf, GenPhase[0], GenPhase[1]);
  and and_3 (IRBuf, GenPhase[0], ~GenPhase[1]);  // AND_Gate
  // AND_Gate and_4 has open pins: in0=GenPhase[0], in1=GenPhase[1], out=open
  and and_5 (PCEn, GenPhase[0], GenPhase[1]);
  assign controlled_buffer_3_out = MARBuf ? Program_counter_q : 16'bz;  // Controlled_Buffer controlled_buffer_3
  assign controlled_buffer_3_out = in_2 ? Accumulator_register_q : 16'bz;  // Controlled_Buffer controlled_buffer_4
  assign controlled_buffer_3_out = IRBuf ? ram_1_data : 16'bz;  // Controlled_Buffer controlled_buffer_5
  assign controlled_buffer_6_out = in_3 ? controlled_buffer_3_out : 16'bz;  // Controlled_Buffer controlled_buffer_6
  assign controlled_buffer_7_out = in_4 ? controlled_buffer_3_out : 16'bz;  // Controlled_Buffer controlled_buffer_7
  assign controlled_buffer_8_out = in_5 ? controlled_buffer_3_out : 16'bz;  // Controlled_Buffer controlled_buffer_8
  assign controlled_buffer_3_out = in_6 ? in_1 : 16'bz;  // Controlled_Buffer controlled_buffer_9
  Register #(.width(16)) Output_register (
    .D(controlled_buffer_8_out), .Q(Output_register_q), .clk(in_8));  // open: en, clr
  Register #(.width(16)) Input_register (
    .D(controlled_buffer_6_out), .en(1'b1), .Q(Input_register_q), .clk(in_8));  // open: clr
  Register #(.width(16)) Input_register_2 (
    .D(controlled_buffer_7_out), .en(1'b1), .Q(Input_register_2_q), .clk(in_8));  // open: clr
  Hex_Digit_Display hex_digit_display_1 (.value(Output_register_q[15:12]));  // open: dp
  ALU alu_1 (.in_1(Input_register_q), .in_2(Input_register_2_q), .in_3(in_7), .out_4(alu_1_out_4));
  Hex_Digit_Display hex_digit_display_2 (.value(Output_register_q[11:8]));  // open: dp
  Hex_Digit_Display hex_digit_display_3 (.value(Output_register_q[7:4]));  // open: dp
  Register #(.width(16)) Accumulator_register (
    .D(alu_1_out_4), .en(1'b1), .Q(Accumulator_register_q), .clk(in_8));  // open: clr
  Hex_Digit_Display hex_digit_display_4 (.value(Output_register_q[3:0]));  // open: dp

  // Other names for the same wires on the sheet: ALU[2:0] = in_7; ALUBuf = in_2; clk = in_8; IBuf = in_6; OBuf = in_5;
  //   PCBuf = MARBuf; RAMBuf = IRBuf; RegBufA = in_3; RegBufB = in_4

  // Notes on the sheet:
  //   PCBuf+MARBuf
  //   RAMBuf+IRBuf
  //   Execute command
  //   PCEN
  //   ROM for control matrix
endmodule
