// Logisim project RAM.circ as structural Verilog: 4 circuits, main circuit RAM
module RAM (
  input  [3:0] Data,
  input  [1:0] Address,
  input  R_W,
  output [3:0] Output
);

  wire memory_cell_1_output, memory_cell_2_output, memory_cell_3_output, memory_cell_4_output,
       memory_cell_5_output, memory_cell_6_output, memory_cell_7_output, memory_cell_8_output,
       memory_cell_9_output, memory_cell_10_output, memory_cell_11_output, memory_cell_12_output,
       memory_cell_13_output, memory_cell_14_output, memory_cell_15_output, memory_cell_16_output,
       n2x4_decoder_1_output_0, n2x4_decoder_1_output_1, n2x4_decoder_1_output_2, n2x4_decoder_1_output_3;

  _2x4_decoder u_2x4_decoder_1 (
    .Input_a(Address[1]), .Input_b(Address[0]), .Output_0(n2x4_decoder_1_output_0),
    .Output_1(n2x4_decoder_1_output_1), .Output_2(n2x4_decoder_1_output_2), .Output_3(n2x4_decoder_1_output_3));
  Memory_cell memory_cell_1 (
    .Select(n2x4_decoder_1_output_0), .Input(Data[3]), .Output(memory_cell_1_output), .R_W(R_W));
  Memory_cell memory_cell_2 (
    .Select(n2x4_decoder_1_output_1), .Input(Data[3]), .Output(memory_cell_2_output), .R_W(R_W));
  Memory_cell memory_cell_3 (
    .Select(n2x4_decoder_1_output_2), .Input(Data[3]), .Output(memory_cell_3_output), .R_W(R_W));
  Memory_cell memory_cell_4 (
    .Select(n2x4_decoder_1_output_3), .Input(Data[3]), .Output(memory_cell_4_output), .R_W(R_W));
  or or_1 (Output[3], memory_cell_1_output, memory_cell_2_output, memory_cell_3_output, memory_cell_4_output);
  Memory_cell memory_cell_5 (
    .Select(n2x4_decoder_1_output_0), .Input(Data[2]), .Output(memory_cell_5_output), .R_W(R_W));
  Memory_cell memory_cell_6 (
    .Select(n2x4_decoder_1_output_1), .Input(Data[2]), .Output(memory_cell_6_output), .R_W(R_W));
  Memory_cell memory_cell_7 (
    .Select(n2x4_decoder_1_output_2), .Input(Data[2]), .Output(memory_cell_7_output), .R_W(R_W));
  Memory_cell memory_cell_8 (
    .Select(n2x4_decoder_1_output_3), .Input(Data[2]), .Output(memory_cell_8_output), .R_W(R_W));
  or or_2 (Output[2], memory_cell_5_output, memory_cell_6_output, memory_cell_7_output, memory_cell_8_output);
  Memory_cell memory_cell_9 (
    .Select(n2x4_decoder_1_output_0), .Input(Data[1]), .Output(memory_cell_9_output), .R_W(R_W));
  Memory_cell memory_cell_10 (
    .Select(n2x4_decoder_1_output_1), .Input(Data[1]), .Output(memory_cell_10_output), .R_W(R_W));
  Memory_cell memory_cell_11 (
    .Select(n2x4_decoder_1_output_2), .Input(Data[1]), .Output(memory_cell_11_output), .R_W(R_W));
  Memory_cell memory_cell_12 (
    .Select(n2x4_decoder_1_output_3), .Input(Data[1]), .Output(memory_cell_12_output), .R_W(R_W));
  or or_3 (Output[1], memory_cell_9_output, memory_cell_10_output, memory_cell_11_output, memory_cell_12_output);
  Memory_cell memory_cell_13 (
    .Select(n2x4_decoder_1_output_0), .Input(Data[0]), .Output(memory_cell_13_output), .R_W(R_W));
  Memory_cell memory_cell_14 (
    .Select(n2x4_decoder_1_output_1), .Input(Data[0]), .Output(memory_cell_14_output), .R_W(R_W));
  Memory_cell memory_cell_15 (
    .Select(n2x4_decoder_1_output_2), .Input(Data[0]), .Output(memory_cell_15_output), .R_W(R_W));
  Memory_cell memory_cell_16 (
    .Select(n2x4_decoder_1_output_3), .Input(Data[0]), .Output(memory_cell_16_output), .R_W(R_W));
  or or_4 (Output[0], memory_cell_13_output, memory_cell_14_output, memory_cell_15_output, memory_cell_16_output);
endmodule

module _2x4_decoder (
  input  Input_a,
  input  Input_b,
  output Output_0,
  output Output_1,
  output Output_2,
  output Output_3
);

  wire not_1_out, not_2_out;

  not not_1 (not_1_out, Input_a);
  not not_2 (not_2_out, Input_b);
  and and_1 (Output_0, not_1_out, not_2_out);
  and and_2 (Output_1, not_1_out, Input_b);
  and and_3 (Output_2, Input_a, not_2_out);
  and and_4 (Output_3, Input_a, Input_b);
endmodule

module Memory_cell (
  input  Select,
  input  Input,
  input  R_W,
  output Output
);

  wire and_1_out, and_2_out, not_1_out, not_2_out, sr_latch_1_output;

  not not_1 (not_1_out, Input);
  and and_1 (and_1_out, Select, not_2_out, not_1_out);
  and and_2 (and_2_out, Select, not_2_out, Input);
  not not_2 (not_2_out, R_W);
  and and_3 (Output, Select, sr_latch_1_output, R_W);
  SR_latch sr_latch_1 (.Set(and_1_out), .Reset(and_2_out), .Output(sr_latch_1_output));
endmodule

module SR_latch (
  input  Set,
  input  Reset,
  output Output
);

  wire nor_2_out;

  nor nor_1 (Output, Set, nor_2_out);
  nor nor_2 (nor_2_out, Output, Reset);
endmodule
